# Fritzing sketch Xentrino-2WD-Teensy 3.2 (saved by Fritzing 0.9.2b)

parts:
  Part1 = Monster Moto Shield
  Teensy_3_1 = Teensy 3.0 [part_number="Freescale ARM MK20DX128"]
  GY2 = MPU-6050 Board GY-521 [form="♀ (female)" package=THT]
  C1 = Capacitor Polarized [package=cpol-radial-10uf-25v]  # not connected
  C2 = Capacitor Polarized [package=cpol-radial-10uf-25v]
  U1 = Voltage Regulator - 5V [package="TO220 [THT]"]
  M1 = DC Motor
  M2 = DC Motor
  Part2 = Lilypad Battery Connect  # not connected

nets:
  N1: Part1.OUTA1, M2.pin_1
  N2: Part1.OUTB1, M2.pin_2
  N3: Part1.OUTA2, M1.pin_1
  N4: Part1.OUTB2, M1.pin_2
  N5: Part1.EN1_-_A0, Teensy_3_1.7
  N6: Part1.EN2_-_A1, Teensy_3_1.8
  N7: Part1.INA2_-_D4, Teensy_3_1.5
  N8: Part1.PWM1_-_D5, Teensy_3_1.4
  N9: Part1.PWM2_-_D6, Teensy_3_1.3
  N10: Part1.INA1_-_D7, Teensy_3_1.2
  N11: Part1.INB2_-_D9, Teensy_3_1.1
  N12: Part1.GND_-_GND@0, Part1.GND_-_GND@1, Part1.GND_-_GND@2
  N13: Teensy_3_1.19, GY2.pin3
  N14: Teensy_3_1.18, Teensy_3_1.17, GY2.pin4
  GND: Teensy_3_1.GND, U1.GND
  N15: C2.-, U1.output_voltage

custom parts:
  MPU-6050 Board GY-521: Acelerometro y Giroscopio MPU-6050 Board GY-521
